# Fritzing sketch MotorTest (saved by Fritzing 0.9.3b)
circuit board: 8.46667cm x 5.64444cm
breadboards: 1

parts:
  DPDT_Relay2 = DPDT Relay [chip_label=Relay package="DIP (Dual Inline) [THT]"]
  DPDT_Relay4 = DPDT Relay [chip_label=Relay package="DIP (Dual Inline) [THT]"]
  DPDT_Relay5 = DPDT Relay [chip_label=Relay package="DIP (Dual Inline) [THT]"]
  DPDT_Relay6 = DPDT Relay [chip_label=Relay package="DIP (Dual Inline) [THT]"]
  J1 = female pin header, 1 pin [form="♀ (female)"]
  J2 = female pin header, 1 pin [form="♀ (female)"]
  J3 = female pin header, 1 pin [form="♀ (female)"]
  J4 = female pin header, 1 pin [form="♀ (female)"]
  J5 = female pin header, 1 pin [form="♀ (female)"]
  J7 = female pin header, 1 pin [form="♀ (female)"]
  J8 = female pin header, 1 pin [form="♀ (female)"]
  J9 = female pin header, 1 pin [form="♀ (female)"]
  J10 = female pin header, 1 pin [form="♀ (female)"]
  J11 = female pin header, 1 pin [form="♀ (female)"]
  J12 = female pin header, 1 pin [form="♀ (female)"]
  J13 = female pin header, 1 pin [form="♀ (female)"]
  J14 = female pin header, 1 pin [form="♀ (female)"]
  DPDT_Relay1 = DPDT Relay [chip_label=Relay package="DIP (Dual Inline) [THT]"]
  D1 = Rectifier Diode [part_number=1N4001 package="300 mil [THT]"]
  D2 = Rectifier Diode [part_number=1N4001 package="300 mil [THT]"]
  D3 = Rectifier Diode [part_number=1N4001 package="300 mil [THT]"]
  D4 = Rectifier Diode [part_number=1N4001 package="300 mil [THT]"]
  D5 = Rectifier Diode [part_number=1N4001 package="300 mil [THT]"]
  D6 = Rectifier Diode [part_number=1N4001 package="300 mil [THT]"]
  Q1 = NPN-Transistor [package="TO92 [THT]"]
  R1 = Resistor [tolerance=±5% resistance=10k package=THT]
  Q2 = NPN-Transistor [package="TO92 [THT]"]
  Q3 = NPN-Transistor [package="TO92 [THT]"]
  Q4 = NPN-Transistor [package="TO92 [THT]"]
  Q5 = NPN-Transistor [package="TO92 [THT]"]
  Q6 = NPN-Transistor [package="TO92 [THT]"]
  R2 = Resistor [tolerance=±5% resistance=10k package=THT]
  R3 = Resistor [tolerance=±5% resistance=10k package=THT]
  R4 = Resistor [tolerance=±5% resistance=10k package=THT]
  R5 = Resistor [tolerance=±5% resistance=10k package=THT]
  R6 = Resistor [tolerance=±5% resistance=10k package=THT]
  DPDT_Relay3 = DPDT Relay [chip_label=Relay package="DIP (Dual Inline) [THT]"]
  J6 = female pin header, 1 pin [form="♀ (female)"]
  J15 = female pin header, 1 pin [form="♀ (female)"]
  J16 = female pin header, 1 pin [form="♀ (female)"]
  R7 = Resistor [tolerance=±5% resistance=1k package=THT]
  J17 = female pin header, 1 pin [form="♀ (female)"]
  R8 = Resistor [tolerance=±5% resistance=1k package=THT]
  J18 = female pin header, 1 pin [form="♀ (female)"]
  J19 = female pin header, 1 pin [form="♀ (female)"]
  J20 = female pin header, 1 pin [form="♀ (female)"]
  J21 = female pin header, 1 pin [form="♀ (female)"]
  J22 = female pin header, 1 pin [form="♀ (female)"]
  J23 = female pin header, 1 pin [form="♀ (female)"]
  J24 = female pin header, 1 pin [form="♀ (female)"]
  J25 = female pin header, 1 pin [form="♀ (female)"]
  J26 = female pin header, 1 pin [form="♀ (female)"]
  J27 = female pin header, 1 pin [form="♀ (female)"]
  J28 = female pin header, 1 pin [form="♀ (female)"]
  J29 = female pin header, 1 pin [form="♀ (female)"]
  R9 = Resistor [tolerance=±5% resistance=1k package=THT]
  R10 = Resistor [tolerance=±5% resistance=1k package=THT]
  R11 = Resistor [tolerance=±5% resistance=1k package=THT]
  R12 = Resistor [tolerance=±5% resistance=1k package=THT]
  R13 = Resistor [tolerance=±5% resistance=1k package=THT]
  R14 = Resistor [tolerance=±5% resistance=1k package=THT]
  R15 = Resistor [tolerance=±5% resistance=1k package=THT]
  R16 = Resistor [tolerance=±5% resistance=1k package=THT]

nets:
  N1: DPDT_Relay2.pin1, DPDT_Relay4.pin1, DPDT_Relay5.pin1, DPDT_Relay6.pin1, DPDT_Relay1.pin1, D1.cathode, D2.cathode, D3.cathode, D4.cathode, D5.cathode, D6.cathode, DPDT_Relay3.pin1, J15.pin1
  N2: DPDT_Relay2.pin5, DPDT_Relay4.pin5, DPDT_Relay5.pin5, J14.pin1, DPDT_Relay1.pin5, DPDT_Relay3.pin5
  N3: DPDT_Relay2.pin6, DPDT_Relay4.pin6, DPDT_Relay5.pin6, DPDT_Relay6.pin5, DPDT_Relay1.pin6, DPDT_Relay3.pin6
  N4: DPDT_Relay2.pin7, J2.pin1, J26.pin1
  N5: DPDT_Relay2.pin8, D2.anode, Q2.C
  N6: DPDT_Relay4.pin7, J4.pin1, J20.pin1
  N7: DPDT_Relay4.pin8, D5.anode, Q4.C
  N8: DPDT_Relay5.pin7, J5.pin1, J16.pin1, R7.Pin_1, J17.pin1
  N9: DPDT_Relay5.pin8, D4.anode, Q5.C
  N10: DPDT_Relay6.pin7, J13.pin1, Q1.E, Q2.E, Q3.E, Q4.E, Q5.E, Q6.E, R8.Pin_0, R9.Pin_0, R11.Pin_0, R13.Pin_0, R15.Pin_0
  N11: DPDT_Relay6.pin8, D6.anode, Q6.C
  N12: J1.pin1, DPDT_Relay1.pin7, J29.pin1
  N13: J3.pin1, DPDT_Relay3.pin7, J23.pin1
  N14: J7.pin1, R2.Pin_0
  N15: J8.pin1, R1.Pin_0
  N16: J9.pin1, R3.Pin_0
  N17: J10.pin1, R4.Pin_0
  N18: J11.pin1, R5.Pin_0
  N19: J12.pin1, R6.Pin_0
  N20: DPDT_Relay1.pin8, D1.anode, Q1.C
  N21: D3.anode, Q3.C, DPDT_Relay3.pin8
  N22: Q1.B, R1.Pin_1
  N23: Q2.B, R2.Pin_1
  N24: Q3.B, R3.Pin_1
  N25: Q4.B, R4.Pin_1
  N26: Q5.B, R5.Pin_1
  N27: Q6.B, R6.Pin_1
  N28: J6.pin1, R7.Pin_0, R8.Pin_1
  N29: J18.pin1, R9.Pin_1, R10.Pin_0
  N30: J19.pin1, R10.Pin_1
  N31: J21.pin1, R11.Pin_1, R12.Pin_0
  N32: J22.pin1, R12.Pin_1
  N33: J24.pin1, R13.Pin_1, R14.Pin_0
  N34: J25.pin1, R14.Pin_1
  N35: J27.pin1, R15.Pin_1, R16.Pin_0
  N36: J28.pin1, R16.Pin_1

custom parts:
  DPDT Relay: DIP DPDT Relay (Double Pole Double Throw)
